# Fritzing sketch PinCode (saved by Fritzing 0.8.3b)
breadboards: 1

parts:
  KEYPAD1 = Membrane Matrix Keypad  # not connected
  Part1 = Arduino Uno (Rev3)
  LCD1 = LCD screen  # not connected
  LED1 = LED - 5mm [color="Red (633nm)" package="5 mm [THT]"]
  LED2 = LED - 5mm [color="Blue (525nm)" package="5 mm [THT]"]
  R1 = Resistor [tolerance=±5% resistance=220 package=THT]
  R2 = Resistor [tolerance=±5% resistance=220 package=THT]

nets:
  N1: Part1.ICSP_MISO, Part1.D12/MISO, LED2.cathode
  N2: Part1.ICSP_SCK, Part1.D13/SCK, LED1.cathode
  N3: Part1.GND, R1.Pin_0, R2.Pin_0
  N4: LED1.anode, R1.Pin_1
  N5: LED2.anode, R2.Pin_1

custom parts:
  Membrane Matrix Keypad: Membrane Matrix 3x4 Keypad
